// Logisim project 1001序列检测.circ as structural Verilog: 1 circuit, main circuit main
module main (
  input  A,
  input  B,
  input  C,
  input  D,
  output F1,
  output F2
);

  wire and_1_out, and_2_out, and_3_out, and_4_out, not_1_out, not_2_out, not_3_out, not_4_out, not_5_out,
       not_6_out, not_7_out;

  not not_1 (not_1_out, A);
  not not_2 (not_2_out, B);
  not not_3 (not_3_out, C);
  and and_1 (and_1_out, not_2_out, not_3_out, not_4_out);
  not not_4 (not_4_out, D);
  not not_5 (not_5_out, B);
  and and_2 (and_2_out, not_5_out, D);
  not not_6 (not_6_out, B);
  and and_3 (and_3_out, not_6_out, C);
  and and_4 (and_4_out, B, not_7_out);
  not not_7 (not_7_out, C);
  or or_1 (F1, not_1_out, and_1_out);
  or or_2 (F2, and_2_out, and_3_out, and_4_out);
endmodule
